// Logisim project Microprocessor.circ as structural Verilog
module FA0 (
  input  in_1,
  input  in_2,
  output out_3,
  output out_4
);

  wire a1_out;

  nor a1 (a1_out, in_1, in_2);
  and c175 (out_4, in_1, in_2);
  nor b1 (out_3, a1_out, out_4);

  // Notes on the sheet:
  //   a
  //   b
  //   Full Adder with C=0
  //   Sarthak Sarans
  //   s275
  //   cout 175
endmodule

module FA1 (
  input  in_1,
  input  in_2,
  output out_3,
  output out_4
);

  wire nand_1_out;

  nand nand_1 (nand_1_out, in_1, in_2);
  or or_1 (out_4, in_1, in_2);
  nand nand_2 (out_3, nand_1_out, out_4);

  // Notes on the sheet:
  //   a
  //   b
  //   Full Adder with C=1
  //   Sarthak Sarans
  //   s275
  //   cout 175
endmodule

module FAopt1 (
  input  in_1,
  input  B,
  input  Cin,
  output a,
  output cout
);

  wire nand_1_out, nand_2_out, nor_1_out, nor_2_out, nor_3_out, not_1_out, not_2_out;

  nor nor_1 (nor_1_out, in_1, B);
  nor nor_2 (nor_2_out, nor_1_out, not_1_out);
  nand nand_1 (nand_1_out, in_1, B);
  not not_1 (not_1_out, nand_1_out);
  nand nand_2 (nand_2_out, nor_2_out, Cin);
  nor nor_3 (nor_3_out, nor_2_out, Cin);
  nand nand_3 (cout, nand_2_out, nand_1_out);
  not not_2 (not_2_out, nand_2_out);
  nor nor_4 (a, nor_3_out, not_2_out);

  // Notes on the sheet:
  //   A
  //   32 transsitors
  //   FAout1 by Sarthak Sarans
  //   5.5 if Cin < 2.75
  //   Cin + 2.75 if Cin > 2.75
  //   4.75 if Cin < 2.75
  //   Cin + 2 if Cin > 2.75
endmodule

module FAopt2 (
  input  in_1,
  input  in_2,
  input  in_3,
  output out_4,
  output out_5
);

  wire and_1_out, nand_1_out, nand_2_out, nand_3_out, nor_1_out, nor_2_out, nor_3_out, not_1_out;

  nor nor_1 (nor_1_out, in_1, in_2);
  not not_1 (not_1_out, nand_1_out);
  nand nand_1 (nand_1_out, in_1, in_2);
  nand nand_2 (nand_2_out, in_2, in_3);
  nand nand_3 (nand_3_out, in_3, in_1);
  nor nor_2 (nor_2_out, nor_1_out, not_1_out);
  nand nand_4 (out_5, nand_1_out, nand_2_out, nand_3_out);
  nor nor_3 (nor_3_out, nor_2_out, in_3);
  and and_1 (and_1_out, nor_2_out, in_3);
  nor nor_4 (out_4, nor_3_out, and_1_out);

  // Notes on the sheet:
  //   Transistors 42
  //   Cin + 2.25
  //   FAout2 by Sarthak Sarans
  //   cout
  //   5.5 if Cin < 2.75
  //   Cin + 2.75 if Cin > 2.75
  //   s
endmodule

module bit4adder0 (
  input  [3:0] in_1,
  input  [3:0] in_2,
  output [3:0] out_3,
  output out_4
);

  wire fa0_1_out_4, faopt1_2_cout, faopt2_1_out_5;

  FAopt1 faopt1_1 (.in_1(in_1[3]), .B(in_2[3]), .Cin(faopt1_2_cout), .cout(out_4), .a(out_3[3]));
  FAopt1 faopt1_2 (.in_1(in_1[2]), .B(in_2[2]), .Cin(faopt2_1_out_5), .cout(faopt1_2_cout), .a(out_3[2]));
  FAopt2 faopt2_1 (.in_1(in_1[1]), .in_2(in_2[1]), .in_3(fa0_1_out_4), .out_5(faopt2_1_out_5), .out_4(out_3[1]));
  FA0 fa0_1 (.in_1(in_1[0]), .in_2(in_2[0]), .out_3(out_3[0]), .out_4(fa0_1_out_4));

  // Notes on the sheet:
  //   8.75
  //   6
  //   6.75
  //   120 Transistors
  //   8.75
  //   4
  //   8
  //   1.75
  //   5.5
  //   2.75
endmodule

module bit4adder1 (
  input  [3:0] in_1,
  input  [3:0] in_2,
  output [3:0] out_3,
  output out_4
);

  wire fa1_1_out_4, faopt1_2_cout, faopt2_1_out_5;

  FAopt1 faopt1_1 (.in_1(in_1[3]), .B(in_2[3]), .Cin(faopt1_2_cout), .cout(out_4), .a(out_3[3]));
  FAopt1 faopt1_2 (.in_1(in_1[2]), .B(in_2[2]), .Cin(faopt2_1_out_5), .cout(faopt1_2_cout), .a(out_3[2]));
  FAopt2 faopt2_1 (.in_1(in_1[1]), .in_2(in_2[1]), .in_3(fa1_1_out_4), .out_5(faopt2_1_out_5), .out_4(out_3[1]));
  FA1 fa1_1 (.in_1(in_1[0]), .in_2(in_2[0]), .out_3(out_3[0]), .out_4(fa1_1_out_4));

  // Notes on the sheet:
  //   8.75
  //   6
  //   6.75
  //   120 Transistors
  //   8.75
  //   4
  //   8
  //   1.75
  //   5.5
  //   2.75
endmodule

module bit8adder (
  input  [7:0] in_1,
  input  [7:0] in_2,
  output [7:0] _16_75
);

  wire fa0_1_out_4, faopt1_1_cout, faopt1_2_cout, faopt1_3_cout, faopt1_4_cout, faopt1_5_cout, faopt1_6_cout,
       faopt2_1_out_5;

  FAopt1 faopt1_1 (.in_1(in_1[7]), .B(in_2[7]), .Cin(faopt1_2_cout), .cout(faopt1_1_cout), .a(_16_75[7]));
  FAopt1 faopt1_2 (.in_1(in_1[6]), .B(in_2[6]), .Cin(faopt1_3_cout), .cout(faopt1_2_cout), .a(_16_75[6]));
  FAopt1 faopt1_3 (.in_1(in_1[5]), .B(in_2[5]), .Cin(faopt1_4_cout), .cout(faopt1_3_cout), .a(_16_75[5]));
  // Probe on faopt1_1_cout
  FAopt1 faopt1_4 (.in_1(in_1[4]), .B(in_2[4]), .Cin(faopt1_5_cout), .cout(faopt1_4_cout), .a(_16_75[4]));
  FAopt1 faopt1_5 (.in_1(in_1[3]), .B(in_2[3]), .Cin(faopt1_6_cout), .cout(faopt1_5_cout), .a(_16_75[3]));
  FAopt1 faopt1_6 (.in_1(in_1[2]), .B(in_2[2]), .Cin(faopt2_1_out_5), .cout(faopt1_6_cout), .a(_16_75[2]));
  FAopt2 faopt2_1 (.in_1(in_1[1]), .in_2(in_2[1]), .in_3(fa0_1_out_4), .out_5(faopt2_1_out_5), .out_4(_16_75[1]));
  FA0 fa0_1 (.in_1(in_1[0]), .in_2(in_2[0]), .out_3(_16_75[0]), .out_4(fa0_1_out_4));

  // Notes on the sheet:
  //   a
  //   b
  //   16
  //   16.75
  //   14
  //   14.75
  //   12
  //   12.75
  //   248 Transistors
  //   10
  //   10.75
  //   16
  //   8
  //   8.75
  //   6
  //   6.75
  //   4
  //   5.5
  //   1.75
  //   2.75
endmodule

module bit8carryselect0 (
  input  [7:0] in_1,
  input  [7:0] in_2,
  output [7:0] out_3,
  output out_4
);

  wire bit4adder0_1_out_4, bit4adder0_2_out_4, bit4adder1_1_out_4, transmissionmux2_1_z;
  wire [3:0] bit4adder0_1_out_3, bit4adder1_1_out_3, mx2i_4_1_out_4;

  transmissionmux2 transmissionmux2_1 (
    .in_1(bit4adder0_1_out_4), .in_2(bit4adder1_1_out_4), .in_3(bit4adder0_2_out_4), .z(transmissionmux2_1_z));
  bit4adder1 bit4adder1_1 (.in_1(in_1[7:4]), .in_2(in_2[7:4]), .out_3(bit4adder1_1_out_3), .out_4(bit4adder1_1_out_4));
  not not_1 (out_4, transmissionmux2_1_z);
  mx2i_4 mx2i_4_1 (
    .in_2(bit4adder1_1_out_3), .in_1(bit4adder0_1_out_3), .in_3(bit4adder0_2_out_4), .out_4(mx2i_4_1_out_4));
  assign out_3[7:4] = ~mx2i_4_1_out_4;  // NOT_Gate not_2, 4 bits wide
  bit4adder0 bit4adder0_1 (.in_1(in_1[7:4]), .in_2(in_2[7:4]), .out_3(bit4adder0_1_out_3), .out_4(bit4adder0_1_out_4));
  bit4adder0 bit4adder0_2 (.in_1(in_1[3:0]), .in_2(in_2[3:0]), .out_3(out_3[3:0]), .out_4(bit4adder0_2_out_4));

  // Notes on the sheet:
  //   8
  //   8.75
  //   10.5
  //   8
  //   9.75
  //   10.5
  //   8.75
  //   8
  //   8.75
endmodule

module bit8carryselect1 (
  input  [7:0] in_1,
  input  [7:0] in_2,
  output [7:0] out_3,
  output out_4
);

  wire bit4adder0_1_out_4, bit4adder1_1_out_4, bit4adder1_2_p1, transmissionmux2_1_z;
  wire [3:0] bit4adder0_1_out_3, bit4adder1_1_out_3, mx2i_4_1_out_4;

  transmissionmux2 transmissionmux2_1 (
    .in_1(bit4adder0_1_out_4), .in_2(bit4adder1_1_out_4), .in_3(bit4adder1_2_p1), .z(transmissionmux2_1_z));
  bit4adder1 bit4adder1_1 (.in_1(in_1[7:4]), .in_2(in_2[7:4]), .out_3(bit4adder1_1_out_3), .out_4(bit4adder1_1_out_4));
  not not_1 (out_4, transmissionmux2_1_z);
  mx2i_4 mx2i_4_1 (
    .in_2(bit4adder1_1_out_3), .in_1(bit4adder0_1_out_3), .in_3(bit4adder1_2_p1), .out_4(mx2i_4_1_out_4));
  assign out_3[7:4] = ~mx2i_4_1_out_4;  // NOT_Gate not_2, 4 bits wide
  bit4adder0 bit4adder0_1 (.in_1(in_1[7:4]), .in_2(in_2[7:4]), .out_3(bit4adder0_1_out_3), .out_4(bit4adder0_1_out_4));
  // bit4adder1 bit4adder1_2: pin names not known; wires that end beside it: bit4adder1_2_p1, in_2[3:0], out_3[3:0], in_1[3:0]

  // Notes on the sheet:
  //   8
  //   8.75
  //   8
  //   8.75
  //   8
  //   8.75
endmodule

module mux2 (
  input  in0,
  input  s,
  input  in_3,
  output z
);

  wire nand_1_out, nand_2_out, not_1_out;

  not not_1 (not_1_out, s);
  nand nand_1 (nand_1_out, in0, not_1_out);
  nand nand_2 (nand_2_out, s, in_3);
  nand nand_3 (z, nand_1_out, nand_2_out);

  // Notes on the sheet:
  //   in1
  //   14 transistors
  //   z=max(s +2.75, in0 + 2 + in1 + 2)
endmodule

module mx2i_4 (
  input  [3:0] in_1,
  input  [3:0] in_2,
  input  in_3,
  output [3:0] out_4
);

  transmissionmux2 transmissionmux2_1 (.in_1(in_1[0]), .in_2(in_2[0]), .in_3(in_3), .z(out_4[0]));
  transmissionmux2 transmissionmux2_2 (.in_1(in_1[1]), .in_2(in_2[1]), .in_3(in_3), .z(out_4[1]));
  transmissionmux2 transmissionmux2_3 (.in_1(in_1[2]), .in_2(in_2[2]), .in_3(in_3), .z(out_4[2]));
  transmissionmux2 transmissionmux2_4 (.in_1(in_1[3]), .in_2(in_2[3]), .in_3(in_3), .z(out_4[3]));
endmodule

module mx2i_8 (
  input  [7:0] in_1,
  input  [7:0] in_2,
  input  in_3,
  output [7:0] out_4
);

  mx2i_4 mx2i_4_1 (.in_2(in_2[3:0]), .in_1(in_1[3:0]), .in_3(in_3), .out_4(out_4[3:0]));
  mx2i_4 mx2i_4_2 (.in_2(in_2[7:4]), .in_1(in_1[7:4]), .in_3(in_3), .out_4(out_4[7:4]));
endmodule

module gatesmux4 (
  input  in_1,
  input  in_2,
  input  in_3,
  input  in_4,
  input  in_5,
  input  in_6,
  output out_7
);

  wire mux2_1_z, mux2_2_z;

  mux2 mux2_1 (.in0(in_1), .s(in_5), .in_3(in_2), .z(mux2_1_z));
  mux2 mux2_2 (.in0(in_3), .s(in_5), .in_3(in_4), .z(mux2_2_z));
  mux2 mux2_3 (.in0(mux2_1_z), .s(in_6), .in_3(mux2_2_z), .z(out_7));

  // Notes on the sheet:
  //   in0
  //   in1
  //   in2
  //   in3
  //   s0
  //   42 transistors
  //   4 input mux with gates
  //   By Sarthak Sarans
  //   s1
  //   z=max(s0 +4.75, s1+2.75, in0 +4, in1 +4, in2+4, in3+4)
  //   z
endmodule

module transmissionmux2 (
  input  in_1,
  input  in_2,
  input  in_3,
  output z
);

  wire not_1_out, transmission_1_p4;

  not not_1 (not_1_out, in_3);
  // Transmission_Gate transmission_1: pin names not known; wires that end beside it: in_1, in_3, not_1_out, transmission_1_p4
  // Transmission_Gate transmission_2: pin names not known; wires that end beside it: in_2, not_1_out, in_3, transmission_1_p4
  not not_2 (z, transmission_1_p4);

  // Notes on the sheet:
  //   in0
  //   in1
  //   sel
  //   8 transistors
  //   z = max(sel + 1.75, in0 + 1, in1 + 1)
endmodule

module transmissionmux4 (
  input  in1,
  input  in_2,
  input  in2,
  input  in_4,
  input  in_5,
  input  in_6,
  output z
);

  wire transmissionmux2_1_z, transmissionmux2_2_z;

  transmissionmux2 transmissionmux2_1 (.in_1(in1), .in_2(in_2), .in_3(in_6), .z(transmissionmux2_1_z));
  transmissionmux2 transmissionmux2_2 (.in_1(in2), .in_2(in_4), .in_3(in_6), .z(transmissionmux2_2_z));
  transmissionmux2 transmissionmux2_3 (.in_1(transmissionmux2_1_z), .in_2(transmissionmux2_2_z), .in_3(in_5), .z(z));

  // Notes on the sheet:
  //   in0
  //   in3
  //   s0
  //   s1
  //   24 transistors
  //   z = max(s0 + 2.75, s1 + 1.75, in0 +2, in1 +2, in2 +2, in3 +2)
endmodule

module bit16carryselect (
  input  [15:0] in_1,
  input  [15:0] in_2,
  output [15:0] out_3,
  output _13
);

  wire bit8carryselect0_1_out_4, bit8carryselect0_2_out_4, bit8carryselect1_1_out_4, transmissionmux2_1_z;
  wire [7:0] bit8carryselect0_1_out_3, bit8carryselect1_1_out_3, mx2i_8_1_out_4;

  transmissionmux2 transmissionmux2_1 (
    .in_1(bit8carryselect0_1_out_4), .in_2(bit8carryselect1_1_out_4), .in_3(bit8carryselect0_2_out_4),
    .z(transmissionmux2_1_z));
  bit8carryselect1 bit8carryselect1_1 (
    .in_2(in_2[15:8]), .in_1(in_1[15:8]), .out_4(bit8carryselect1_1_out_4), .out_3(bit8carryselect1_1_out_3));
  not not_1 (_13, transmissionmux2_1_z);
  bit8carryselect0 bit8carryselect0_1 (
    .in_2(in_2[15:8]), .in_1(in_1[15:8]), .out_3(bit8carryselect0_1_out_3), .out_4(bit8carryselect0_1_out_4));
  mx2i_8 mx2i_8_1 (
    .in_1(bit8carryselect0_1_out_3), .in_2(bit8carryselect1_1_out_3), .in_3(bit8carryselect0_2_out_4),
    .out_4(mx2i_8_1_out_4));
  assign out_3[15:8] = ~mx2i_8_1_out_4;  // NOT_Gate not_2, 8 bits wide
  bit8carryselect0 bit8carryselect0_2 (
    .in_2(in_2[7:0]), .in_1(in_1[7:0]), .out_3(out_3[7:0]), .out_4(bit8carryselect0_2_out_4));

  // Notes on the sheet:
  //   10.5
  //   10.5
  //   12.25
  //   10.5
  //   10.5
  //   10.5
  //   12.25
  //   13
endmodule

module addsub1 (
  input  in_1,
  input  [15:0] in_2,
  input  [15:0] in_3,
  output [15:0] out_4,
  output out_5
);

  wire nand_1_out, nand_2_out, not_2_out, not_3_out, not_4_out;
  wire [15:0] multiplexer_1_out, not_1_out;

  Multiplexer #(.width(16)) multiplexer_1 (.in0(in_3), .in1(not_1_out), .out(multiplexer_1_out), .sel(in_1));
  assign not_1_out = ~in_3;  // NOT_Gate not_1, 16 bits wide
  Adder #(.width(16)) adder_1 (.a(in_2), .b(multiplexer_1_out), .out(out_4), .cin(in_1));  // open: cout
  not not_2 (not_2_out, out_4[15]);
  not not_3 (not_3_out, in_2[15]);
  not not_4 (not_4_out, multiplexer_1_out[15]);
  nand nand_1 (nand_1_out, not_2_out, in_2[15], multiplexer_1_out[15]);
  nand nand_2 (nand_2_out, not_3_out, not_4_out, out_4[15]);
  nand nand_3 (out_5, nand_1_out, nand_2_out);
endmodule

module carryselect4pt2 (
  input  [3:0] in_1,
  input  [3:0] in_2,
  input  in_3,
  output [3:0] out_4,
  output out_5
);

  wire faopt1_2_cout, faopt2_1_out_5, faopt2_2_out_5;

  FAopt1 faopt1_1 (.in_1(in_1[3]), .B(in_2[3]), .Cin(faopt1_2_cout), .cout(out_5), .a(out_4[3]));
  FAopt1 faopt1_2 (.in_1(in_1[2]), .B(in_2[2]), .Cin(faopt2_1_out_5), .cout(faopt1_2_cout), .a(out_4[2]));
  FAopt2 faopt2_1 (.in_1(in_1[1]), .in_2(in_2[1]), .in_3(faopt2_2_out_5), .out_5(faopt2_1_out_5), .out_4(out_4[1]));
  FAopt2 faopt2_2 (.in_1(in_1[0]), .in_2(in_2[0]), .in_3(in_3), .out_5(faopt2_2_out_5), .out_4(out_4[0]));

  // Notes on the sheet:
  //   8.75
  //   6
  //   6.75
  //   120 Transistors
  //   8.75
  //   4
  //   8
  //   1.75
  //   5.5
  //   2.75
endmodule

module carryselect8pt2 (
  input  [7:0] in_1,
  input  [7:0] in_2,
  input  in_3,
  output [7:0] out_4,
  output out_5
);

  wire bit4adder0_1_out_4, bit4adder1_1_out_4, carryselect4pt2_1_out_5, transmissionmux2_1_z;
  wire [3:0] bit4adder0_1_out_3, bit4adder1_1_out_3, mx2i_4_1_out_4;

  transmissionmux2 transmissionmux2_1 (
    .in_1(bit4adder0_1_out_4), .in_2(bit4adder1_1_out_4), .in_3(carryselect4pt2_1_out_5),
    .z(transmissionmux2_1_z));
  bit4adder1 bit4adder1_1 (.in_1(in_1[7:4]), .in_2(in_2[7:4]), .out_3(bit4adder1_1_out_3), .out_4(bit4adder1_1_out_4));
  not not_1 (out_5, transmissionmux2_1_z);
  mx2i_4 mx2i_4_1 (
    .in_2(bit4adder1_1_out_3), .in_1(bit4adder0_1_out_3), .in_3(carryselect4pt2_1_out_5),
    .out_4(mx2i_4_1_out_4));
  assign out_4[7:4] = ~mx2i_4_1_out_4;  // NOT_Gate not_2, 4 bits wide
  bit4adder0 bit4adder0_1 (.in_1(in_1[7:4]), .in_2(in_2[7:4]), .out_3(bit4adder0_1_out_3), .out_4(bit4adder0_1_out_4));
  carryselect4pt2 carryselect4pt2_1 (
    .in_3(in_3), .in_1(in_1[3:0]), .in_2(in_2[3:0]), .out_4(out_4[3:0]), .out_5(carryselect4pt2_1_out_5));

  // Notes on the sheet:
  //   8
  //   8.75
  //   8
  //   10.5
  //   9.75
  //   8.75
  //   10.5
  //   8
  //   8.75
endmodule

module carrselcet16p2 (
  input  [15:0] in_1,
  input  [15:0] in_2,
  input  in_3,
  output [15:0] out_4,
  output _13
);

  wire bit8carryselect0_1_out_4, bit8carryselect1_1_out_4, carryselect8pt2_1_out_5, transmissionmux2_1_z;
  wire [7:0] bit8carryselect0_1_out_3, bit8carryselect1_1_out_3, mx2i_8_1_out_4;

  transmissionmux2 transmissionmux2_1 (
    .in_1(bit8carryselect0_1_out_4), .in_2(bit8carryselect1_1_out_4), .in_3(carryselect8pt2_1_out_5),
    .z(transmissionmux2_1_z));
  bit8carryselect1 bit8carryselect1_1 (
    .in_2(in_2[15:8]), .in_1(in_1[15:8]), .out_4(bit8carryselect1_1_out_4), .out_3(bit8carryselect1_1_out_3));
  not not_1 (_13, transmissionmux2_1_z);
  bit8carryselect0 bit8carryselect0_1 (
    .in_2(in_2[15:8]), .in_1(in_1[15:8]), .out_3(bit8carryselect0_1_out_3), .out_4(bit8carryselect0_1_out_4));
  mx2i_8 mx2i_8_1 (
    .in_1(bit8carryselect0_1_out_3), .in_2(bit8carryselect1_1_out_3), .in_3(carryselect8pt2_1_out_5),
    .out_4(mx2i_8_1_out_4));
  assign out_4[15:8] = ~mx2i_8_1_out_4;  // NOT_Gate not_2, 8 bits wide
  carryselect8pt2 carryselect8pt2_1 (
    .in_3(in_3), .in_2(in_2[7:0]), .in_1(in_1[7:0]), .out_5(carryselect8pt2_1_out_5), .out_4(out_4[7:0]));

  // Notes on the sheet:
  //   10.5
  //   10.5
  //   12.25
  //   10.5
  //   10.5
  //   10.5
  //   12.25
  //   13
endmodule

module addsub2 (
  input  in_1,
  input  [15:0] in_2,
  input  [15:0] in_3,
  output [15:0] out_4,
  output out_5
);

  wire nand_1_out, nand_2_out, not_2_out, not_3_out, not_4_out;
  wire [15:0] multiplexer_1_out, not_1_out;

  Multiplexer #(.width(16)) multiplexer_1 (.in0(in_3), .in1(not_1_out), .out(multiplexer_1_out), .sel(in_1));
  assign not_1_out = ~in_3;  // NOT_Gate not_1, 16 bits wide
  carrselcet16p2 carrselcet16p2_1 (.in_3(in_1), .in_1(in_2), .in_2(multiplexer_1_out), .out_4(out_4));  // open: _13
  not not_2 (not_2_out, out_4[15]);
  not not_3 (not_3_out, in_2[15]);
  not not_4 (not_4_out, multiplexer_1_out[15]);
  nand nand_1 (nand_1_out, not_2_out, in_2[15], multiplexer_1_out[15]);
  nand nand_2 (nand_2_out, not_3_out, not_4_out, out_4[15]);
  nand nand_3 (out_5, nand_1_out, nand_2_out);
endmodule

module registers (
  input  rst,
  input  sub_input,
  input  [15:0] in_3
);

  wire clk;
  wire [15:0] addsub1_1_out_4, R0, R1;

  Clock clock_1 (.out(clk));
  Register #(.width(16)) u_R0 (.D(addsub1_1_out_4), .en(1'b1), .clk(clk), .Q(R0), .clr(rst));
  Register #(.width(16)) u_R1 (.D(in_3), .en(1'b1), .clk(clk), .Q(R1), .clr(rst));
  Hex_Digit_Display hex_digit_display_1 (.value(R0[15:12]));  // open: dp
  Hex_Digit_Display hex_digit_display_2 (.value(R0[11:8]));  // open: dp
  Hex_Digit_Display hex_digit_display_3 (.value(R0[7:4]));  // open: dp
  Hex_Digit_Display hex_digit_display_4 (.value(R0[3:0]));  // open: dp
  Hex_Digit_Display hex_digit_display_5 (.value(R1[15:12]));  // open: dp
  Hex_Digit_Display hex_digit_display_6 (.value(R1[11:8]));  // open: dp
  Hex_Digit_Display hex_digit_display_7 (.value(R1[7:4]));  // open: dp
  addsub1 addsub1_1 (.in_1(sub_input), .in_2(R0), .in_3(R1), .out_4(addsub1_1_out_4));  // open: out_5
  Hex_Digit_Display hex_digit_display_8 (.value(R1[3:0]));  // open: dp

  // Notes on the sheet:
  //   5 for add and 4 for sub
endmodule

module resigisters2 (
  input  rst,
  input  [1:0] in_2,
  input  [1:0] in_3,
  input  sub_input,
  input  in_5
);

  wire clk, ovrfl, reg0WE, reg1WE, reg2WE, reg3WE, register_1_q;
  wire [15:0] a, addsub1_1_out_4, b, R0, R1, R2, R3;

  Clock clock_1 (.out(clk));
  Hex_Digit_Display hex_digit_display_1 (.value(R0[15:12]));  // open: dp
  Hex_Digit_Display hex_digit_display_2 (.value(R2[15:12]));  // open: dp
  Hex_Digit_Display hex_digit_display_3 (.value(R2[11:8]));  // open: dp
  srcSel srcsel_1 (.in_1(in_2), .in_2(R0), .in_3(R1), .in_4(R2), .in_5(R3), .out_6(a));
  srcSel srcsel_2 (.in_1(in_3), .in_2(R0), .in_3(R1), .in_4(R2), .in_5(R3), .out_6(b));
  Hex_Digit_Display hex_digit_display_4 (.value(R0[11:8]));  // open: dp
  Hex_Digit_Display hex_digit_display_5 (.value(R0[7:4]));  // open: dp
  Hex_Digit_Display hex_digit_display_6 (.value(R2[7:4]));  // open: dp
  Hex_Digit_Display hex_digit_display_7 (.value(R2[3:0]));  // open: dp
  Hex_Digit_Display hex_digit_display_8 (.value(R0[3:0]));  // open: dp
  Hex_Digit_Display hex_digit_display_9 (.value(R1[15:12]));  // open: dp
  Hex_Digit_Display hex_digit_display_10 (.value(R3[15:12]));  // open: dp
  Hex_Digit_Display hex_digit_display_11 (.value(R3[11:8]));  // open: dp
  Hex_Digit_Display hex_digit_display_12 (.value(R1[11:8]));  // open: dp
  Hex_Digit_Display hex_digit_display_13 (.value(R1[7:4]));  // open: dp
  Hex_Digit_Display hex_digit_display_14 (.value(R3[7:4]));  // open: dp
  Hex_Digit_Display hex_digit_display_15 (.value(R3[3:0]));  // open: dp
  Register #(.width(1)) register_1 (.D(1'b1), .en(ovrfl), .clk(clk), .Q(register_1_q), .clr(rst));
  addsub1 addsub1_1 (.in_1(sub_input), .in_2(a), .in_3(b), .out_4(addsub1_1_out_4), .out_5(ovrfl));
  Hex_Digit_Display hex_digit_display_16 (.value(R1[3:0]));  // open: dp
  regWE regwe_1 (.in_2(in_5), .in_1(in_2), .out_3(reg0WE), .out_4(reg1WE), .out_5(reg2WE), .out_6(reg3WE));
  LED led_1 (.in(register_1_q));
  Register #(.width(16)) register_2 (.D(addsub1_1_out_4), .en(reg0WE), .clk(clk), .Q(R0), .clr(rst));
  Register #(.width(16)) register_3 (.D(addsub1_1_out_4), .en(reg1WE), .clk(clk), .Q(R1), .clr(rst));
  Register #(.width(16)) register_4 (.D(addsub1_1_out_4), .en(reg2WE), .clk(clk), .Q(R2), .clr(rst));
  Register #(.width(16)) register_5 (.D(addsub1_1_out_4), .en(reg3WE), .clk(clk), .Q(R3), .clr(rst));

  // Other names for the same wires on the sheet: Rd[1:0] = in_2; Rs[1:0] = in_3

  // Notes on the sheet:
  //   4c41
  //   5341
  //   7B43
  //   537D
endmodule

module regWE (
  input  [1:0] in_1,
  input  in_2,
  output out_3,
  output out_4,
  output out_5,
  output out_6
);

  wire not_1_out, not_2_out, not_3_out;

  not not_1 (not_1_out, in_2);
  not not_2 (not_2_out, in_1[1]);
  not not_3 (not_3_out, in_1[0]);
  nor nor_1 (out_3, in_1[0], in_1[1], not_1_out);
  and and_1 (out_4, in_1[0], not_2_out, in_2);
  and and_2 (out_5, not_3_out, in_1[1], in_2);
  and and_3 (out_6, in_1[0], in_1[1], in_2);
endmodule

module srcSel (
  input  [1:0] in_1,
  input  [15:0] in_2,
  input  [15:0] in_3,
  input  [15:0] in_4,
  input  [15:0] in_5,
  output [15:0] out_6
);

  Multiplexer #(.select(2), .width(16)) multiplexer_1 (
    .in0(in_2), .in1(in_3), .in2(in_4), .in3(in_5), .out(out_6), .sel(in_1));
endmodule

module firstprogram (
  input  rst
);

  wire clk, not_1_out, not_2_out, opcode, ovrfl, reg0WE, reg1WE, reg2WE, reg3WE, register_1_q;
  wire [1:0] Rd, Rs;
  wire [3:0] ram_1_dout;
  wire [5:0] programcounter_1_out_3;
  wire [15:0] a, addsub1_1_out_4, b, R0, R1, R2, R3;

  Clock clock_1 (.out(clk));
  Hex_Digit_Display hex_digit_display_1 (.value(R0[15:12]));  // open: dp
  Hex_Digit_Display hex_digit_display_2 (.value(R0[11:8]));  // open: dp
  Hex_Digit_Display hex_digit_display_3 (.value(R2[15:12]));  // open: dp
  Hex_Digit_Display hex_digit_display_4 (.value(R2[11:8]));  // open: dp
  srcSel srcsel_1 (.in_1(Rd), .in_2(R0), .in_3(R1), .in_4(R2), .in_5(R3), .out_6(a));
  srcSel srcsel_2 (.in_1(Rs), .in_2(R0), .in_3(R1), .in_4(R2), .in_5(R3), .out_6(b));
  Hex_Digit_Display hex_digit_display_5 (.value(R0[7:4]));  // open: dp
  Hex_Digit_Display hex_digit_display_6 (.value(R0[3:0]));  // open: dp
  Hex_Digit_Display hex_digit_display_7 (.value(R2[7:4]));  // open: dp
  Hex_Digit_Display hex_digit_display_8 (.value(R2[3:0]));  // open: dp
  Hex_Digit_Display hex_digit_display_9 (.value(R1[15:12]));  // open: dp
  Hex_Digit_Display hex_digit_display_10 (.value(R1[11:8]));  // open: dp
  Hex_Digit_Display hex_digit_display_11 (.value(R3[15:12]));  // open: dp
  Hex_Digit_Display hex_digit_display_12 (.value(R3[11:8]));  // open: dp
  Register #(.width(1)) register_1 (.D(1'b1), .en(ovrfl), .clk(clk), .Q(register_1_q), .clr(rst));
  Hex_Digit_Display hex_digit_display_13 (.value(R1[7:4]));  // open: dp
  Hex_Digit_Display hex_digit_display_14 (.value(R1[3:0]));  // open: dp
  Hex_Digit_Display hex_digit_display_15 (.value(R3[7:4]));  // open: dp
  Hex_Digit_Display hex_digit_display_16 (.value(R3[3:0]));  // open: dp
  regWE regwe_1 (.in_2(1'b1), .in_1(Rd), .out_3(reg0WE), .out_4(reg1WE), .out_5(reg2WE), .out_6(reg3WE));
  LED led_1 (.in(register_1_q));
  addsub1 addsub1_1 (.in_1(opcode), .in_2(a), .in_3(b), .out_4(addsub1_1_out_4), .out_5(ovrfl));
  Register #(.width(16)) u_R0 (.D(addsub1_1_out_4), .en(reg0WE), .clk(clk), .Q(R0), .clr(rst));
  Register #(.width(16)) u_R1 (.D(addsub1_1_out_4), .en(reg1WE), .clk(clk), .Q(R1), .clr(rst));
  Register #(.width(16)) u_R2 (.D(addsub1_1_out_4), .en(reg2WE), .clk(clk), .Q(R2), .clr(rst));
  Register #(.width(16)) u_R3 (.D(addsub1_1_out_4), .en(reg3WE), .clk(clk), .Q(R3), .clr(rst));
  programcounter programcounter_1 (.clk(clk), .rst(rst), .out_3(programcounter_1_out_3));
  RAM #(.addrWidth(6), .asyncread("true"), .trigger("falling")) ram_1 (
    .addr(programcounter_1_out_3), .we(1'b0), .oe(1'b1), .clk(clk), .dout({Rd, Rs, ram_1_dout}));  // open: din
  not not_1 (not_1_out, ram_1_dout[3]);
  not not_2 (not_2_out, ram_1_dout[2]);
  and and_1 (opcode, not_1_out, not_2_out, ram_1_dout[1], ram_1_dout[0]);

  // Notes on the sheet:
  //   4c41
  //   5341
  //   7B43
  //   537D
endmodule

module programcounter (
  input  clk,
  input  rst,
  output [5:0] out_3
);

  wire [5:0] adder_1_out;

  Register #(.width(6)) PC (.D(adder_1_out), .en(1'b1), .clk(clk), .Q(out_3), .clr(rst));
  Adder #(.width(6)) adder_1 (.a(out_3), .b(6'b000001), .out(adder_1_out));  // open: cin, cout

  // Other names for the same wires on the sheet: R0[5:0] = out_3
endmodule

module firstprogramv2 (
  input  rst
);

  wire clk, d_ff_1_q, delay, opcode, ovrfl, reg0WE, reg1WE, reg2WE, reg3WE, register_1_q;
  wire [1:0] Rd, Rs;
  wire [5:0] programcounter_1_out_3;
  wire [7:0] InstructionRegister_q, ram_1_dout;
  wire [15:0] a, addsub1_1_out_4, b, R0, R1, R2, R3;

  Clock clock_1 (.out(clk));
  srcSel srcsel_1 (.in_1(Rd), .in_2(R0), .in_3(R1), .in_4(R2), .in_5(R3), .out_6(a));
  srcSel srcsel_2 (.in_1(Rs), .in_2(R0), .in_3(R1), .in_4(R2), .in_5(R3), .out_6(b));
  regWE regwe_1 (.in_2(delay), .in_1(Rd), .out_3(reg0WE), .out_4(reg1WE), .out_5(reg2WE), .out_6(reg3WE));
  Hex_Digit_Display hex_digit_display_1 (.value(R0[15:12]));  // open: dp
  Hex_Digit_Display hex_digit_display_2 (.value(R2[15:12]));  // open: dp
  Hex_Digit_Display hex_digit_display_3 (.value(R2[11:8]));  // open: dp
  Hex_Digit_Display hex_digit_display_4 (.value(R0[11:8]));  // open: dp
  Hex_Digit_Display hex_digit_display_5 (.value(R0[7:4]));  // open: dp
  Hex_Digit_Display hex_digit_display_6 (.value(R2[7:4]));  // open: dp
  Hex_Digit_Display hex_digit_display_7 (.value(R2[3:0]));  // open: dp
  Register #(.width(1)) register_1 (.D(delay), .en(ovrfl), .clk(clk), .Q(register_1_q), .clr(rst));
  Hex_Digit_Display hex_digit_display_8 (.value(R0[3:0]));  // open: dp
  D_Flip_Flop d_ff_1 (.D(1'b1), .clk(clk), .Q(d_ff_1_q), .reset(rst));  // open: Qn, preset
  Hex_Digit_Display hex_digit_display_9 (.value(R1[15:12]));  // open: dp
  Hex_Digit_Display hex_digit_display_10 (.value(R3[15:12]));  // open: dp
  Hex_Digit_Display hex_digit_display_11 (.value(R3[11:8]));  // open: dp
  LED led_1 (.in(register_1_q));
  Hex_Digit_Display hex_digit_display_12 (.value(R1[11:8]));  // open: dp
  Hex_Digit_Display hex_digit_display_13 (.value(R1[7:4]));  // open: dp
  Hex_Digit_Display hex_digit_display_14 (.value(R3[7:4]));  // open: dp
  Hex_Digit_Display hex_digit_display_15 (.value(R3[3:0]));  // open: dp
  D_Flip_Flop d_ff_2 (.D(d_ff_1_q), .clk(clk), .Q(delay), .reset(rst));  // open: Qn, preset
  addsub1 addsub1_1 (.in_1(opcode), .in_2(a), .in_3(b), .out_4(addsub1_1_out_4), .out_5(ovrfl));
  Hex_Digit_Display hex_digit_display_16 (.value(R1[3:0]));  // open: dp
  Register #(.width(16)) u_R0 (.D(addsub1_1_out_4), .en(reg0WE), .clk(clk), .Q(R0), .clr(rst));
  Register #(.width(16)) u_R1 (.D(addsub1_1_out_4), .en(reg1WE), .clk(clk), .Q(R1), .clr(rst));
  Register #(.width(16)) u_R2 (.D(addsub1_1_out_4), .en(reg2WE), .clk(clk), .Q(R2), .clr(rst));
  Register #(.width(16)) u_R3 (.D(addsub1_1_out_4), .en(reg3WE), .clk(clk), .Q(R3), .clr(rst));
  programcounter programcounter_1 (.clk(clk), .rst(rst), .out_3(programcounter_1_out_3));
  RAM #(.addrWidth(6), .asyncread("true"), .trigger("falling")) ram_1 (
    .addr(programcounter_1_out_3), .we(1'b0), .oe(1'b1), .clk(clk), .dout(ram_1_dout));  // open: din
  Register InstructionRegister (.D(ram_1_dout), .en(1'b1), .clk(clk), .Q(InstructionRegister_q), .clr(rst));
  IRDecoder irdecoder_1 (.in_1(InstructionRegister_q), .clk(clk), .rst(rst), .op(opcode), .Rs(Rs), .Rd(Rd));

  // Notes on the sheet:
  //   4c41
  //   5341
  //   7B43
  //   537D
endmodule

module IRDecoder (
  input  [7:0] in_1,
  input  clk,
  input  rst,
  output op,
  output [1:0] Rs,
  output [1:0] Rd
);

  wire and_1_out, not_1_out, not_2_out;

  not not_1 (not_1_out, in_1[2]);
  not not_2 (not_2_out, in_1[3]);
  and and_1 (and_1_out, in_1[0], in_1[1], not_2_out, not_1_out);
  D_Flip_Flop d_ff_1 (.D(and_1_out), .clk(clk), .Q(op), .reset(rst));  // open: Qn, preset
  Register #(.width(2)) register_1 (.D(in_1[5:4]), .en(1'b1), .clk(clk), .Q(Rs), .clr(rst));
  Register #(.width(2)) register_2 (.D(in_1[7:6]), .en(1'b1), .clk(clk), .Q(Rd), .clr(rst));
endmodule

module IRDecoderv2 (
  input  [7:0] in_1,
  input  clk,
  input  rst,
  output op,
  output Ldi,
  output ld,
  output [1:0] Rs,
  output [1:0] Rd
);

  wire and_1_out, and_2_out, and_3_out, not_1_out, not_2_out, not_3_out;

  not not_1 (not_1_out, in_1[3]);
  not not_2 (not_2_out, in_1[3]);
  not not_3 (not_3_out, in_1[0]);
  and and_1 (and_1_out, in_1[3], not_3_out, in_1[1], in_1[3]);
  Register #(.width(2)) register_1 (.D(in_1[5:4]), .en(1'b1), .clk(clk), .Q(Rs), .clr(rst));
  Register #(.width(2)) register_2 (.D(in_1[7:6]), .en(1'b1), .clk(clk), .Q(Rd), .clr(rst));
  and and_2 (and_2_out, in_1[0], not_1_out, in_1[1], not_2_out);
  and and_3 (and_3_out, in_1[3], in_1[3], in_1[1], in_1[0]);
  D_Flip_Flop d_ff_1 (.D(and_2_out), .clk(clk), .Q(op), .reset(rst));  // open: Qn, preset
  D_Flip_Flop d_ff_2 (.D(and_1_out), .clk(clk), .Q(Ldi), .reset(rst));  // open: Qn, preset
  D_Flip_Flop d_ff_3 (.D(and_3_out), .clk(clk), .Q(ld), .reset(rst));  // open: Qn, preset

  assign in_1[2] = in_1[3];
endmodule

module LoadingData (
  input  rst,
  output [15:0] out_2
);

  wire clk, d_ff_1_q, delay, ld, ldi, opcode, ovrfl, reg0WE, reg1WE, reg2WE, reg3WE, register_1_q;
  wire [1:0] Rd;
  wire [5:0] programcounter_1_out_3;
  wire [7:0] ache_dout, InstructionRegister_q;
  wire [15:0] a, b, DataRAM_dout, multiplexer_1_out, mux2, output1, R0, R1, R2, R3;

  Clock clock_1 (.out(clk));
  srcSel srcsel_1 (.in_1(Rd), .in_2(R0), .in_3(R1), .in_4(R2), .in_5(R3), .out_6(a));
  srcSel srcsel_2 (.in_1(out_2[1:0]), .in_2(R0), .in_3(R1), .in_4(R2), .in_5(R3), .out_6(b));
  regWE regwe_1 (.in_2(delay), .in_1(Rd), .out_3(reg0WE), .out_4(reg1WE), .out_5(reg2WE), .out_6(reg3WE));
  Hex_Digit_Display hex_digit_display_1 (.value(R0[15:12]));  // open: dp
  Hex_Digit_Display hex_digit_display_2 (.value(R2[15:12]));  // open: dp
  Hex_Digit_Display hex_digit_display_3 (.value(R2[11:8]));  // open: dp
  Hex_Digit_Display hex_digit_display_4 (.value(R0[11:8]));  // open: dp
  Hex_Digit_Display hex_digit_display_5 (.value(R0[7:4]));  // open: dp
  Hex_Digit_Display hex_digit_display_6 (.value(R2[7:4]));  // open: dp
  Hex_Digit_Display hex_digit_display_7 (.value(R2[3:0]));  // open: dp
  Register #(.width(1)) register_1 (.D(delay), .en(ovrfl), .clk(clk), .Q(register_1_q), .clr(rst));
  Hex_Digit_Display hex_digit_display_8 (.value(R0[3:0]));  // open: dp
  D_Flip_Flop d_ff_1 (.D(1'b1), .clk(clk), .Q(d_ff_1_q), .reset(rst));  // open: Qn, preset
  Hex_Digit_Display hex_digit_display_9 (.value(R1[15:12]));  // open: dp
  Hex_Digit_Display hex_digit_display_10 (.value(R3[15:12]));  // open: dp
  Hex_Digit_Display hex_digit_display_11 (.value(R3[11:8]));  // open: dp
  LED led_1 (.in(register_1_q));
  Hex_Digit_Display hex_digit_display_12 (.value(R1[11:8]));  // open: dp
  Hex_Digit_Display hex_digit_display_13 (.value(R1[7:4]));  // open: dp
  Hex_Digit_Display hex_digit_display_14 (.value(R3[7:4]));  // open: dp
  Hex_Digit_Display hex_digit_display_15 (.value(R3[3:0]));  // open: dp
  D_Flip_Flop d_ff_2 (.D(d_ff_1_q), .clk(clk), .Q(delay), .reset(rst));  // open: Qn, preset
  addsub1 addsub1_1 (.in_1(opcode), .in_2(a), .in_3(b), .out_4(mux2), .out_5(ovrfl));
  Hex_Digit_Display hex_digit_display_16 (.value(R1[3:0]));  // open: dp
  Register #(.width(16)) u_R0 (.D(output1), .en(reg0WE), .clk(clk), .Q(R0), .clr(rst));
  Register #(.width(16)) u_R1 (.D(output1), .en(reg1WE), .clk(clk), .Q(R1), .clr(rst));
  Register #(.width(16)) u_R2 (.D(output1), .en(reg2WE), .clk(clk), .Q(R2), .clr(rst));
  Register #(.width(16)) u_R3 (.D(output1), .en(reg3WE), .clk(clk), .Q(R3), .clr(rst));
  programcounter programcounter_1 (.clk(clk), .rst(rst), .out_3(programcounter_1_out_3));
  RAM #(.addrWidth(6), .asyncread("true"), .trigger("falling")) ache (
    .addr(programcounter_1_out_3), .we(1'b0), .oe(1'b1), .clk(clk), .dout(ache_dout));  // open: din
  RAM #(.addrWidth(4), .asyncread("true"), .dataWidth(16), .trigger("falling")) DataRAM (
    .addr(b[3:0]), .we(1'b0), .oe(clk), .clk(clk), .dout(DataRAM_dout));  // open: din
  Register InstructionRegister (.D(ache_dout), .en(1'b1), .clk(clk), .Q(InstructionRegister_q), .clr(rst));
  Multiplexer #(.width(16)) multiplexer_1 (.in0(mux2), .in1(DataRAM_dout), .out(multiplexer_1_out), .sel(ld));
  Multiplexer #(.width(16)) multiplexer_2 (
    .in0(multiplexer_1_out), .in1({{14{1'b0}}, out_2[1:0]}), .out(output1), .sel(ldi));
  IRDecoderv2 irdecoderv2_1 (
    .in_1(InstructionRegister_q), .clk(clk), .rst(rst), .op(opcode), .Ldi(ldi), .ld(ld), .Rs(out_2[1:0]),
    .Rd(Rd));

  assign out_2[15:2] = {14{1'b0}};

  // Other names for the same wires on the sheet: Rs[1:0] = out_2[1:0]

  // Notes on the sheet:
  //   4c41
  //   5341
  //   7B43
  //   537D
  //   Cache
endmodule

module IRDecoderv3 (
  input  [7:0] in_1,
  input  clk,
  input  rst,
  output op,
  output Ldi,
  output ld,
  output [1:0] Rs,
  output [1:0] Rd,
  output move,
  output store
);

  wire and_1_out, and_2_out, and_3_out, and_4_out, and_5_out, not_1_out, not_2_out, not_3_out, not_4_out,
       not_5_out, not_6_out;

  not not_1 (not_1_out, in_1[2]);
  not not_2 (not_2_out, in_1[3]);
  not not_3 (not_3_out, in_1[0]);
  not not_4 (not_4_out, in_1[3]);
  not not_5 (not_5_out, in_1[2]);
  not not_6 (not_6_out, in_1[0]);
  and and_1 (and_1_out, in_1[2], not_6_out, in_1[1], in_1[3]);
  Register #(.width(2)) register_1 (.D(in_1[5:4]), .en(1'b1), .clk(clk), .Q(Rs), .clr(rst));
  Register #(.width(2)) register_2 (.D(in_1[7:6]), .en(1'b1), .clk(clk), .Q(Rd), .clr(rst));
  and and_2 (and_2_out, not_3_out, in_1[1], in_1[2], not_4_out);
  and and_3 (and_3_out, in_1[0], in_1[1], not_5_out, in_1[3]);
  and and_4 (and_4_out, in_1[0], not_1_out, in_1[1], not_2_out);
  and and_5 (and_5_out, in_1[3], in_1[2], in_1[1], in_1[0]);
  D_Flip_Flop d_ff_1 (.D(and_2_out), .clk(clk), .Q(move), .reset(rst));  // open: Qn, preset
  D_Flip_Flop d_ff_2 (.D(and_3_out), .clk(clk), .Q(store), .reset(rst));  // open: Qn, preset
  D_Flip_Flop d_ff_3 (.D(and_4_out), .clk(clk), .Q(op), .reset(rst));  // open: Qn, preset
  D_Flip_Flop d_ff_4 (.D(and_1_out), .clk(clk), .Q(Ldi), .reset(rst));  // open: Qn, preset
  D_Flip_Flop d_ff_5 (.D(and_5_out), .clk(clk), .Q(ld), .reset(rst));  // open: Qn, preset
endmodule

module StoringData (
  input  rst,
  output [15:0] out_2
);

  wire clk, d_ff_1_q, delay, ld, ldi, move, multiplexer_1_out, opcode, ovrfl, reg0WE, reg1WE, reg2WE, reg3WE,
       register_1_q, store;
  wire [1:0] Rd;
  wire [5:0] programcounter_1_out_3;
  wire [7:0] ache_dout, InstructionRegister_q;
  wire [15:0] a, b, DataRAM_dout, multiplexer_2_out, multiplexer_3_out, output1, R0, R1, R2, R3, sum;

  Multiplexer multiplexer_1 (.in0(delay), .in1(1'b0), .out(multiplexer_1_out), .sel(store));
  Clock clock_1 (.out(clk));
  srcSel srcsel_1 (.in_1(Rd), .in_2(R0), .in_3(R1), .in_4(R2), .in_5(R3), .out_6(a));
  srcSel srcsel_2 (.in_1(out_2[1:0]), .in_2(R0), .in_3(R1), .in_4(R2), .in_5(R3), .out_6(b));
  regWE regwe_1 (.in_2(multiplexer_1_out), .in_1(Rd), .out_3(reg0WE), .out_4(reg1WE), .out_5(reg2WE), .out_6(reg3WE));
  Hex_Digit_Display hex_digit_display_1 (.value(R0[15:12]));  // open: dp
  Hex_Digit_Display hex_digit_display_2 (.value(R2[15:12]));  // open: dp
  Hex_Digit_Display hex_digit_display_3 (.value(R0[11:8]));  // open: dp
  Hex_Digit_Display hex_digit_display_4 (.value(R0[7:4]));  // open: dp
  Hex_Digit_Display hex_digit_display_5 (.value(R2[11:8]));  // open: dp
  Hex_Digit_Display hex_digit_display_6 (.value(R2[7:4]));  // open: dp
  Hex_Digit_Display hex_digit_display_7 (.value(R0[3:0]));  // open: dp
  Hex_Digit_Display hex_digit_display_8 (.value(R2[3:0]));  // open: dp
  Register #(.width(1)) register_1 (.D(delay), .en(ovrfl), .clk(clk), .Q(register_1_q), .clr(rst));
  Hex_Digit_Display hex_digit_display_9 (.value(R1[15:12]));  // open: dp
  Hex_Digit_Display hex_digit_display_10 (.value(R3[15:12]));  // open: dp
  LED led_1 (.in(register_1_q));
  D_Flip_Flop d_ff_1 (.D(1'b1), .clk(clk), .Q(d_ff_1_q), .reset(rst));  // open: Qn, preset
  Hex_Digit_Display hex_digit_display_11 (.value(R1[11:8]));  // open: dp
  Hex_Digit_Display hex_digit_display_12 (.value(R1[7:4]));  // open: dp
  Hex_Digit_Display hex_digit_display_13 (.value(R3[11:8]));  // open: dp
  Hex_Digit_Display hex_digit_display_14 (.value(R3[7:4]));  // open: dp
  D_Flip_Flop d_ff_2 (.D(d_ff_1_q), .clk(clk), .Q(delay), .reset(rst));  // open: Qn, preset
  addsub1 addsub1_1 (.in_1(opcode), .in_2(a), .in_3(b), .out_4(sum), .out_5(ovrfl));
  Hex_Digit_Display hex_digit_display_15 (.value(R1[3:0]));  // open: dp
  Hex_Digit_Display hex_digit_display_16 (.value(R3[3:0]));  // open: dp
  Register #(.width(16)) u_R0 (.D(output1), .en(reg0WE), .clk(clk), .Q(R0), .clr(rst));
  Register #(.width(16)) u_R1 (.D(output1), .en(reg1WE), .clk(clk), .Q(R1), .clr(rst));
  Register #(.width(16)) u_R2 (.D(output1), .en(reg2WE), .clk(clk), .Q(R2), .clr(rst));
  Register #(.width(16)) u_R3 (.D(output1), .en(reg3WE), .clk(clk), .Q(R3), .clr(rst));
  programcounter programcounter_1 (.clk(clk), .rst(rst), .out_3(programcounter_1_out_3));
  RAM #(.addrWidth(6), .asyncread("true"), .trigger("falling")) ache (
    .addr(programcounter_1_out_3), .we(1'b0), .oe(1'b1), .clk(clk), .dout(ache_dout));  // open: din
  RAM #(.addrWidth(4), .asyncread("true"), .dataWidth(16), .trigger("falling")) DataRAM (
    .addr(b[3:0]), .we(store), .oe(clk), .clk(clk), .din(a), .dout(DataRAM_dout));
  Register InstructionRegister (.D(ache_dout), .en(1'b1), .clk(clk), .Q(InstructionRegister_q), .clr(rst));
  Multiplexer #(.width(16)) multiplexer_2 (.in0(sum), .in1(DataRAM_dout), .out(multiplexer_2_out), .sel(ld));
  Multiplexer #(.width(16)) multiplexer_3 (
    .in0(multiplexer_2_out), .in1({{14{1'b0}}, out_2[1:0]}), .out(multiplexer_3_out), .sel(ldi));
  Multiplexer #(.width(16)) multiplexer_4 (.in0(multiplexer_3_out), .in1(b), .out(output1), .sel(move));
  IRDecoderv3 irdecoderv3_1 (
    .in_1(InstructionRegister_q), .clk(clk), .rst(rst), .op(opcode), .Ldi(ldi), .ld(ld), .Rs(out_2[1:0]),
    .Rd(Rd), .move(move), .store(store));

  assign out_2[15:2] = {14{1'b0}};

  // Other names for the same wires on the sheet: Rs[1:0] = out_2[1:0]

  // Notes on the sheet:
  //   Cache
endmodule

module IRDecoderV4 (
  input  [7:0] in_1,
  input  clk,
  input  rst,
  output op,
  output Ldi,
  output ld,
  output [1:0] Rs,
  output [1:0] Rd,
  output move,
  output store,
  output jump,
  output [5:0] targ,
  output halt
);

  wire and_1_out, and_2_out, and_3_out, and_4_out, and_5_out, and_6_out, and_7_out, d_ff_6_q, not_1_out,
       not_2_out, not_3_out, not_4_out, not_5_out, not_6_out, not_7_out, not_8_out, not_9_out, not_10_out;

  not not_1 (not_1_out, in_1[2]);
  not not_2 (not_2_out, in_1[3]);
  not not_3 (not_3_out, in_1[0]);
  not not_4 (not_4_out, in_1[1]);
  not not_5 (not_5_out, in_1[0]);
  not not_6 (not_6_out, in_1[3]);
  not not_7 (not_7_out, in_1[2]);
  and and_1 (and_1_out, not_3_out, not_4_out);
  not not_8 (not_8_out, in_1[0]);
  not not_9 (not_9_out, in_1[3]);
  not not_10 (not_10_out, in_1[0]);
  and and_2 (and_2_out, in_1[2], not_10_out, in_1[1], in_1[3]);
  Register #(.width(2)) register_1 (.D(in_1[5:4]), .en(1'b1), .clk(clk), .Q(Rs), .clr(rst));
  Register #(.width(2)) register_2 (.D(in_1[7:6]), .en(1'b1), .clk(clk), .Q(Rd), .clr(rst));
  and and_3 (and_3_out, not_5_out, in_1[1], in_1[2], not_6_out);
  and and_4 (and_4_out, in_1[0], in_1[1], not_7_out, in_1[3]);
  D_Flip_Flop d_ff_1 (.D(and_5_out), .clk(clk), .Q(halt), .reset(rst));  // open: Qn, preset
  and and_5 (and_5_out, in_1[4], in_1[5], in_1[2], in_1[1], not_8_out, not_9_out, in_1[6], in_1[7]);
  and and_6 (and_6_out, in_1[0], not_1_out, in_1[1], not_2_out);
  and and_7 (and_7_out, in_1[3], in_1[2], in_1[1], in_1[0]);
  D_Flip_Flop d_ff_2 (.D(and_3_out), .clk(clk), .Q(move), .reset(rst));  // open: Qn, preset
  D_Flip_Flop d_ff_3 (.D(and_4_out), .clk(clk), .Q(store), .reset(rst));  // open: Qn, preset
  D_Flip_Flop d_ff_4 (.D(and_6_out), .clk(clk), .Q(op), .reset(rst));  // open: Qn, preset
  D_Flip_Flop d_ff_5 (.D(and_2_out), .clk(clk), .Q(Ldi), .reset(rst));  // open: Qn, preset
  D_Flip_Flop d_ff_6 (.D(1'b1), .clk(clk), .Q(d_ff_6_q), .reset(rst));  // open: Qn, preset
  D_Flip_Flop d_ff_7 (.D(and_7_out), .clk(clk), .Q(ld), .reset(rst));  // open: Qn, preset
  and and_8 (jump, and_1_out, d_ff_6_q);

  assign targ = in_1[7:2];
endmodule

module JumpingData (
  input  rst,
  output [15:0] out_2,
  output [15:0] cycles
);

  wire clk, d_ff_1_q, d_ff_2_q, delay, halt, jump, ld, ldi, move, multiplexer_1_out, opcode, or_1_out, ovrfl,
       reg0WE, reg1WE, reg2WE, reg3WE, register_1_q, store;
  wire [1:0] Rd;
  wire [5:0] programcounterv2_1_pc2, targ;
  wire [7:0] ache_dout, InstructionRegister_q;
  wire [15:0] a, b, DataRAM_dout, multiplexer_2_out, multiplexer_3_out, output1, R0, R1, R2, R3, sum;

  or or_1 (or_1_out, store, d_ff_1_q);
  Multiplexer multiplexer_1 (.in0(delay), .in1(1'b0), .out(multiplexer_1_out), .sel(or_1_out));
  D_Flip_Flop d_ff_1 (.D(jump), .clk(clk), .Q(d_ff_1_q), .reset(rst));  // open: Qn, preset
  Clock clock_1 (.out(clk));
  srcSel srcsel_1 (.in_1(Rd), .in_2(R0), .in_3(R1), .in_4(R2), .in_5(R3), .out_6(a));
  srcSel srcsel_2 (.in_1(out_2[1:0]), .in_2(R0), .in_3(R1), .in_4(R2), .in_5(R3), .out_6(b));
  regWE regwe_1 (.in_2(multiplexer_1_out), .in_1(Rd), .out_3(reg0WE), .out_4(reg1WE), .out_5(reg2WE), .out_6(reg3WE));
  Hex_Digit_Display hex_digit_display_1 (.value(R0[15:12]));  // open: dp
  Hex_Digit_Display hex_digit_display_2 (.value(R2[15:12]));  // open: dp
  Hex_Digit_Display hex_digit_display_3 (.value(R0[11:8]));  // open: dp
  Hex_Digit_Display hex_digit_display_4 (.value(R0[7:4]));  // open: dp
  Hex_Digit_Display hex_digit_display_5 (.value(R2[11:8]));  // open: dp
  Hex_Digit_Display hex_digit_display_6 (.value(R2[7:4]));  // open: dp
  Hex_Digit_Display hex_digit_display_7 (.value(R0[3:0]));  // open: dp
  Hex_Digit_Display hex_digit_display_8 (.value(R2[3:0]));  // open: dp
  Register #(.width(1)) register_1 (.D(delay), .en(ovrfl), .clk(clk), .Q(register_1_q), .clr(rst));
  Hex_Digit_Display hex_digit_display_9 (.value(R1[15:12]));  // open: dp
  Hex_Digit_Display hex_digit_display_10 (.value(R3[15:12]));  // open: dp
  LED led_1 (.in(register_1_q));
  D_Flip_Flop d_ff_2 (.D(1'b1), .clk(clk), .Q(d_ff_2_q), .reset(rst));  // open: Qn, preset
  Hex_Digit_Display hex_digit_display_11 (.value(R1[11:8]));  // open: dp
  Hex_Digit_Display hex_digit_display_12 (.value(R1[7:4]));  // open: dp
  Hex_Digit_Display hex_digit_display_13 (.value(R3[11:8]));  // open: dp
  Hex_Digit_Display hex_digit_display_14 (.value(R3[7:4]));  // open: dp
  D_Flip_Flop d_ff_3 (.D(d_ff_2_q), .clk(clk), .Q(delay), .reset(rst));  // open: Qn, preset
  addsub1 addsub1_1 (.in_1(opcode), .in_2(a), .in_3(b), .out_4(sum), .out_5(ovrfl));
  Hex_Digit_Display hex_digit_display_15 (.value(R1[3:0]));  // open: dp
  Hex_Digit_Display hex_digit_display_16 (.value(R3[3:0]));  // open: dp
  Register #(.width(16)) u_R0 (.D(output1), .en(reg0WE), .clk(clk), .Q(R0), .clr(rst));
  Register #(.width(16)) u_R1 (.D(output1), .en(reg1WE), .clk(clk), .Q(R1), .clr(rst));
  Register #(.width(16)) u_R2 (.D(output1), .en(reg2WE), .clk(clk), .Q(R2), .clr(rst));
  Register #(.width(16)) u_R3 (.D(output1), .en(reg3WE), .clk(clk), .Q(R3), .clr(rst));
  programCounterv2 programcounterv2_1 (.clk(clk), .rst(rst), .Targ(targ), .jump(jump), .PC2(programcounterv2_1_pc2));
  RAM #(.addrWidth(6), .asyncread("true"), .trigger("falling")) ache (
    .addr(programcounterv2_1_pc2), .we(1'b0), .oe(1'b1), .clk(clk), .dout(ache_dout));  // open: din
  RAM #(.addrWidth(4), .asyncread("true"), .dataWidth(16), .trigger("falling")) DataRAM (
    .addr(b[3:0]), .we(store), .oe(clk), .clk(clk), .din(a), .dout(DataRAM_dout));
  Register InstructionRegister (.D(ache_dout), .en(1'b1), .clk(clk), .Q(InstructionRegister_q), .clr(rst));
  CycleCounter cyclecounter_1 (.clk(clk), .rst(rst), .halt(halt), .cycles(cycles));
  Multiplexer #(.width(16)) multiplexer_2 (.in0(sum), .in1(DataRAM_dout), .out(multiplexer_2_out), .sel(ld));
  Multiplexer #(.width(16)) multiplexer_3 (
    .in0(multiplexer_2_out), .in1({{14{1'b0}}, out_2[1:0]}), .out(multiplexer_3_out), .sel(ldi));
  Multiplexer #(.width(16)) multiplexer_4 (.in0(multiplexer_3_out), .in1(b), .out(output1), .sel(move));
  IRDecoderV4 irdecoderv4_1 (
    .in_1(InstructionRegister_q), .clk(clk), .rst(rst), .op(opcode), .Ldi(ldi), .ld(ld), .Rs(out_2[1:0]),
    .Rd(Rd), .move(move), .store(store), .jump(jump), .targ(targ), .halt(halt));

  assign out_2[15:2] = {14{1'b0}};

  // Other names for the same wires on the sheet: Rs[1:0] = out_2[1:0]

  // Notes on the sheet:
  //   Cache
endmodule

module programCounterv2 (
  input  clk,
  input  rst,
  input  [5:0] Targ,
  input  jump,
  output [5:0] PC2
);

  wire [5:0] adder_1_out, multiplexer_1_out;

  Register #(.width(6)) PC (.D(multiplexer_1_out), .en(1'b1), .clk(clk), .Q(PC2), .clr(rst));
  Adder #(.width(6)) adder_1 (.a(PC2), .b(6'b000001), .out(adder_1_out));  // open: cin, cout
  Multiplexer #(.width(6)) multiplexer_1 (.in0(adder_1_out), .in1(Targ), .out(multiplexer_1_out), .sel(jump));
endmodule

module CycleCounter (
  input  clk,
  input  rst,
  input  halt,
  output [15:0] cycles
);

  wire not_1_out, register_1_q;
  wire [15:0] adder_1_out;

  Adder #(.width(16)) adder_1 (.a(cycles), .b(16'h1), .out(adder_1_out));  // open: cin, cout
  Register #(.width(1)) register_1 (.D(1'b1), .en(halt), .clk(clk), .Q(register_1_q), .clr(rst));
  Register #(.width(16)) HW (.D(adder_1_out), .en(not_1_out), .clk(clk), .Q(cycles), .clr(rst));
  not not_1 (not_1_out, register_1_q);
endmodule

module FinalMicroprocessor (
  input  rst,
  output [15:0] out_2,
  output [15:0] cycles
);

  wire and_1_out, and_2_out, and_3_out, clk, CondJmp, d_ff_1_q, delay, halt, jmp, jmpn, ld, ldi, move,
       multiplexer_1_out, not_1_out, not_2_out, not_3_out, ofl, opcode, or_1_out, or_2_out, or_3_out, ovrfl,
       reg0WE, reg1WE, reg2WE, reg3WE, register_1_q, register_2_q, register_3_q, store;
  wire [1:0] Rd;
  wire [5:0] programcounterv2_1_pc2, targ;
  wire [7:0] ache_dout, InstructionRegister_q;
  wire [15:0] a, b, DataRAM_dout, multiplexer_2_out, multiplexer_3_out, output1, R0, R1, R2, R3, sum;

  or or_1 (or_1_out, store, register_1_q, register_2_q);
  Register #(.width(1)) register_1 (.D(jmp), .en(1'b1), .clk(clk), .Q(register_1_q), .clr(rst));
  Multiplexer multiplexer_1 (.in0(delay), .in1(1'b0), .out(multiplexer_1_out), .sel(or_1_out));
  Clock clock_1 (.out(clk));
  Register #(.width(1)) register_2 (.D(jmpn), .en(1'b1), .clk(clk), .Q(register_2_q), .clr(rst));
  srcSel srcsel_1 (.in_1(Rd), .in_2(R0), .in_3(R1), .in_4(R2), .in_5(R3), .out_6(a));
  srcSel srcsel_2 (.in_1(out_2[1:0]), .in_2(R0), .in_3(R1), .in_4(R2), .in_5(R3), .out_6(b));
  regWE regwe_1 (.in_2(multiplexer_1_out), .in_1(Rd), .out_3(reg0WE), .out_4(reg1WE), .out_5(reg2WE), .out_6(reg3WE));
  Hex_Digit_Display hex_digit_display_1 (.value(R0[15:12]));  // open: dp
  Hex_Digit_Display hex_digit_display_2 (.value(R2[15:12]));  // open: dp
  Hex_Digit_Display hex_digit_display_3 (.value(R0[11:8]));  // open: dp
  Hex_Digit_Display hex_digit_display_4 (.value(R0[7:4]));  // open: dp
  Hex_Digit_Display hex_digit_display_5 (.value(R2[11:8]));  // open: dp
  Hex_Digit_Display hex_digit_display_6 (.value(R2[7:4]));  // open: dp
  not not_1 (not_1_out, a[15]);
  not not_2 (not_2_out, b[15]);
  Hex_Digit_Display hex_digit_display_7 (.value(R0[3:0]));  // open: dp
  Hex_Digit_Display hex_digit_display_8 (.value(R2[3:0]));  // open: dp
  Register #(.width(1)) register_3 (.D(delay), .en(ofl), .clk(clk), .Q(register_3_q), .clr(rst));
  and and_1 (and_1_out, a[15], b[15]);
  and and_2 (and_2_out, not_1_out, not_2_out);
  or or_2 (or_2_out, jmp, CondJmp);
  Hex_Digit_Display hex_digit_display_9 (.value(R1[15:12]));  // open: dp
  Hex_Digit_Display hex_digit_display_10 (.value(R3[15:12]));  // open: dp
  LED led_1 (.in(register_3_q));
  D_Flip_Flop d_ff_1 (.D(1'b1), .clk(clk), .Q(d_ff_1_q), .reset(rst));  // open: Qn, preset
  Hex_Digit_Display hex_digit_display_11 (.value(R1[11:8]));  // open: dp
  Hex_Digit_Display hex_digit_display_12 (.value(R1[7:4]));  // open: dp
  Hex_Digit_Display hex_digit_display_13 (.value(R3[11:8]));  // open: dp
  Hex_Digit_Display hex_digit_display_14 (.value(R3[7:4]));  // open: dp
  D_Flip_Flop d_ff_2 (.D(d_ff_1_q), .clk(clk), .Q(delay), .reset(rst));  // open: Qn, preset
  or or_3 (or_3_out, and_1_out, and_2_out);
  not not_3 (not_3_out, opcode);
  addsub1 addsub1_1 (.in_1(opcode), .in_2(a), .in_3(b), .out_4(sum), .out_5(ovrfl));
  Hex_Digit_Display hex_digit_display_15 (.value(R1[3:0]));  // open: dp
  Hex_Digit_Display hex_digit_display_16 (.value(R3[3:0]));  // open: dp
  and and_3 (and_3_out, or_3_out, not_3_out);
  and and_4 (ofl, ovrfl, and_3_out);
  Register #(.width(16)) u_R0 (.D(output1), .en(reg0WE), .clk(clk), .Q(R0), .clr(rst));
  Register #(.width(16)) u_R1 (.D(output1), .en(reg1WE), .clk(clk), .Q(R1), .clr(rst));
  Register #(.width(16)) u_R2 (.D(output1), .en(reg2WE), .clk(clk), .Q(R2), .clr(rst));
  Register #(.width(16)) u_R3 (.D(output1), .en(reg3WE), .clk(clk), .Q(R3), .clr(rst));
  programCounterv2 programcounterv2_1 (
    .clk(clk), .rst(rst), .Targ(targ), .jump(or_2_out), .PC2(programcounterv2_1_pc2));
  RAM #(.addrWidth(6), .asyncread("true"), .trigger("falling")) ache (
    .addr(programcounterv2_1_pc2), .we(1'b0), .oe(1'b1), .clk(clk), .dout(ache_dout));  // open: din
  RAM #(.addrWidth(7), .asyncread("true"), .dataWidth(16), .trigger("falling")) DataRAM (
    .addr(b[6:0]), .we(store), .oe(clk), .clk(clk), .din(a), .dout(DataRAM_dout));
  Register InstructionRegister (.D(ache_dout), .en(1'b1), .clk(clk), .Q(InstructionRegister_q), .clr(rst));
  CycleCounter cyclecounter_1 (.clk(clk), .rst(rst), .halt(halt), .cycles(cycles));
  Multiplexer #(.width(16)) multiplexer_2 (.in0(sum), .in1(DataRAM_dout), .out(multiplexer_2_out), .sel(ld));
  Multiplexer #(.width(16)) multiplexer_3 (
    .in0(multiplexer_2_out), .in1({{14{1'b0}}, out_2[1:0]}), .out(multiplexer_3_out), .sel(ldi));
  Multiplexer #(.width(16)) multiplexer_4 (.in0(multiplexer_3_out), .in1(b), .out(output1), .sel(move));
  IRDecorderV5 irdecorderv5_1 (
    .in_1(InstructionRegister_q), .clk(clk), .rst(rst), .op(opcode), .Ldi(ldi), .ld(ld), .Rs(out_2[1:0]),
    .Rd(Rd), .move(move), .store(store), .jmp(jmp), .targ(targ), .halt(halt), .jmpn(jmpn));
  and and_5 (CondJmp, output1[15], jmpn);

  assign out_2[15:2] = {14{1'b0}};

  // Other names for the same wires on the sheet: Rs[1:0] = out_2[1:0]

  // Notes on the sheet:
  //   Cache
endmodule

module IRDecorderV5 (
  input  [7:0] in_1,
  input  clk,
  input  rst,
  output op,
  output Ldi,
  output ld,
  output [1:0] Rs,
  output [1:0] Rd,
  output move,
  output store,
  output jmp,
  output [5:0] targ,
  output halt,
  output jmpn
);

  wire and_1_out, and_3_out, and_4_out, and_5_out, and_6_out, and_7_out, and_8_out, d_ff_6_q, not_1_out,
       not_2_out, not_3_out, not_4_out, not_5_out, not_6_out, not_7_out, not_8_out, not_9_out, not_10_out,
       not_11_out;

  not not_1 (not_1_out, in_1[2]);
  not not_2 (not_2_out, in_1[3]);
  not not_3 (not_3_out, in_1[0]);
  not not_4 (not_4_out, in_1[1]);
  not not_5 (not_5_out, in_1[0]);
  not not_6 (not_6_out, in_1[3]);
  not not_7 (not_7_out, in_1[2]);
  and and_1 (and_1_out, not_3_out, not_4_out);
  not not_8 (not_8_out, in_1[0]);
  not not_9 (not_9_out, in_1[3]);
  and and_2 (jmpn, in_1[0], not_10_out);
  not not_10 (not_10_out, in_1[1]);
  not not_11 (not_11_out, in_1[0]);
  and and_3 (and_3_out, in_1[2], not_11_out, in_1[1], in_1[3]);
  Register #(.width(2)) register_1 (.D(in_1[5:4]), .en(1'b1), .clk(clk), .Q(Rs), .clr(rst));
  Register #(.width(2)) register_2 (.D(in_1[7:6]), .en(1'b1), .clk(clk), .Q(Rd), .clr(rst));
  and and_4 (and_4_out, not_5_out, in_1[1], in_1[2], not_6_out);
  and and_5 (and_5_out, in_1[0], in_1[1], not_7_out, in_1[3]);
  D_Flip_Flop d_ff_1 (.D(and_6_out), .clk(clk), .Q(halt), .reset(rst));  // open: Qn, preset
  and and_6 (and_6_out, in_1[4], in_1[5], in_1[2], in_1[1], not_8_out, not_9_out, in_1[6], in_1[7]);
  and and_7 (and_7_out, in_1[0], not_1_out, in_1[1], not_2_out);
  and and_8 (and_8_out, in_1[3], in_1[2], in_1[1], in_1[0]);
  D_Flip_Flop d_ff_2 (.D(and_4_out), .clk(clk), .Q(move), .reset(rst));  // open: Qn, preset
  D_Flip_Flop d_ff_3 (.D(and_5_out), .clk(clk), .Q(store), .reset(rst));  // open: Qn, preset
  D_Flip_Flop d_ff_4 (.D(and_7_out), .clk(clk), .Q(op), .reset(rst));  // open: Qn, preset
  D_Flip_Flop d_ff_5 (.D(and_3_out), .clk(clk), .Q(Ldi), .reset(rst));  // open: Qn, preset
  D_Flip_Flop d_ff_6 (.D(1'b1), .clk(clk), .Q(d_ff_6_q), .reset(rst));  // open: Qn, preset
  D_Flip_Flop d_ff_7 (.D(and_8_out), .clk(clk), .Q(ld), .reset(rst));  // open: Qn, preset
  and and_9 (jmp, and_1_out, d_ff_6_q);

  assign targ = in_1[7:2];
endmodule
